// Digital circuit CPU.dig as structural Verilog
module CPU (
  input  CLK,
  output [7:0] HI,
  output [7:0] LO
);

  wire AluSrc, and_1_out, and_2_out, BNE, Branch, JAL, JR, Jump, LUI, MemRead, MemtoReg, MemWrite, MFEN,
       nand_1_out, RegDst, RegWrite, u_ALU_zero, WRITELOHI;
  wire [1:0] SLIHO;
  wire [2:0] FUNCT, Instruction_Memory_d_2, Instruction_Memory_d_3, multiplexer_2_out, multiplexer_3_out;
  wire [3:0] AluOp, OPCODE;
  wire [5:3] Instruction_Memory_d;
  wire [7:0] add_1_s, add_2_s, add_3_s, bitextender_1_out, DA, Data_Memory_d, multiplexer_1_out,
       multiplexer_4_out, multiplexer_5_out, multiplexer_6_out, multiplexer_7_out, multiplexer_9_out,
       multiplexer_10_out, multiplexer_11_out, PC, Registers_db, u_ALU_high, u_ALU_s;

  Add #(.Bits(8)) add_1 (.a(8'h1), .b(PC), .c_i(1'b0), .s(add_1_s));  // open: c_o
  Register #(.Bits(8), .isProgramCounter("true")) u_PC (.D(multiplexer_1_out), .C(CLK), .en(CLK), .Q(PC));
  ROM #(.AddrBits(8), .isProgramMemory("true"), .Bits(16)) Instruction_Memory (
    .A(PC), .sel(1'b1),
    .D({OPCODE, Instruction_Memory_d_3, Instruction_Memory_d_2, Instruction_Memory_d, FUNCT}));
  Multiplexer #(.Bits(8)) multiplexer_1 (.sel(JR), .in_0(multiplexer_5_out), .in_1(DA), .out(multiplexer_1_out));
  LookUpTable #(.Bits(18)) CONTROLLER (
    .in0(FUNCT[0]), .in1(FUNCT[1]), .in2(FUNCT[2]), .in3(OPCODE[0]), .in4(OPCODE[1]), .in5(OPCODE[2]),
    .in6(OPCODE[3]),
    .out({JAL, LUI, MFEN, JR, BNE, WRITELOHI, MemRead, AluOp, Jump, Branch, MemWrite, RegWrite, MemtoReg, AluSrc, RegDst}));
  Multiplexer #(.Bits(3)) multiplexer_2 (
    .sel(RegDst), .in_0(Instruction_Memory_d), .in_1(Instruction_Memory_d_2), .out(multiplexer_2_out));
  BitExtender #(.inputBits(6), .outputBits(8)) bitextender_1 (
    .in({Instruction_Memory_d, FUNCT}), .out(bitextender_1_out));
  Add #(.Bits(8)) add_2 (.a(add_1_s), .b(bitextender_1_out), .c_i(1'b0), .s(add_2_s));  // open: c_o
  Multiplexer #(.Bits(3)) multiplexer_3 (.sel(JAL), .in_0(multiplexer_2_out), .in_1(3'b111), .out(multiplexer_3_out));
  Multiplexer #(.Bits(8)) multiplexer_4 (.sel(and_1_out), .in_0(add_1_s), .in_1(add_2_s), .out(multiplexer_4_out));
  Multiplexer #(.Bits(8)) multiplexer_5 (
    .sel(Jump), .in_0(multiplexer_4_out), .in_1({Instruction_Memory_d_2[1:0], Instruction_Memory_d, FUNCT}),
    .out(multiplexer_5_out));
  RegisterFile #(.AddrBits(3), .Bits(8)) Registers (
    .Din(multiplexer_9_out), .we(RegWrite), .Rw(multiplexer_3_out), .C(CLK), .Ra(Instruction_Memory_d_3),
    .Rb(Instruction_Memory_d_2), .Da(DA), .Db(Registers_db));
  Multiplexer #(.Bits(8)) multiplexer_6 (
    .sel(LUI), .in_0(bitextender_1_out), .in_1({bitextender_1_out[3:0], 4'b0000}), .out(multiplexer_6_out));
  and and_1 (and_1_out, nand_1_out, Branch);
  nand nand_1 (nand_1_out, BNE, u_ALU_zero);
  Multiplexer #(.Bits(8)) multiplexer_7 (
    .sel(AluSrc), .in_0(Registers_db), .in_1(multiplexer_6_out), .out(multiplexer_7_out));
  ALU #(.applicationType("IVERILOG"), .CodeFile("/home/doruk/circuits/SRC/ALU.v")) u_ALU (
    .ALUop(AluOp), .A(DA), .B(multiplexer_7_out), .SHAMT(Instruction_Memory_d_3), .S(u_ALU_s),
    .HIGH(u_ALU_high), .Zero(u_ALU_zero));
  Multiplexer #(.Bits(2)) multiplexer_8 (.sel(MFEN), .in_0(2'b00), .in_1(FUNCT[2:1]), .out(SLIHO));
  and and_2 (and_2_out, 1'b1, WRITELOHI);
  Register #(.Bits(8)) u_LO (.D(u_ALU_s), .C(CLK), .en(and_2_out), .Q(LO));
  Register #(.Bits(8)) u_HI (.D(u_ALU_high), .C(CLK), .en(and_2_out), .Q(HI));
  Multiplexer #(.Selector_Bits(2), .Bits(8)) multiplexer_9 (
    .sel(SLIHO), .in_0(multiplexer_10_out), .in_1(multiplexer_10_out), .in_2(HI), .in_3(LO),
    .out(multiplexer_9_out));
  RAMDualPort #(.AddrBits(8), .Bits(8)) Data_Memory (
    .A(u_ALU_s), .Din(Registers_db), .str(MemWrite), .C(CLK), .ld(MemRead), .D(Data_Memory_d));
  Multiplexer #(.Bits(8)) multiplexer_10 (
    .sel(JAL), .in_0(multiplexer_11_out), .in_1(add_3_s), .out(multiplexer_10_out));
  Multiplexer #(.Bits(8)) multiplexer_11 (
    .sel(MemtoReg), .in_0(u_ALU_s), .in_1(Data_Memory_d), .out(multiplexer_11_out));
  Add #(.Bits(8)) add_3 (.a(PC), .b(8'h1), .c_i(1'b0), .s(add_3_s));  // open: c_o

  // Other names for the same wires on the sheet: C = CLK

  // Notes on the sheet:
  //   contents of Instruction_Memory (hex, n*v repeats v):
  //   7054,708a,229a,50c1,7045
  //   ADDR
  //   OPCODE
  //   8 bits of Address
  //   IMM
  //   RT
  //   RS
  //   FUNCT
  //   RD
  //   contents of CONTROLLER (hex, n*v repeats v):
  //   0,588,608,688,4000,8008,8008,8,8,88,88,388,408,1200,1200,1280
  //   ,1300,488,708,208,508,0,0,0,8*40,8*20048,8*a0,8*20a0,16*b,16*70b
  //   ,8*38b,8*40b,8*1040b,8*80f,8*12
  //   RegDst
endmodule
